// Logisim project branch-comp.circ as structural Verilog: 1 circuit, main circuit branch_comp
module branch_comp (
  input  [31:0] BrData1,
  input  [31:0] BrData2,
  input  BrUn,
  output BrEq,
  output BrLt
);

  wire BrEqS, BrEqUn, BrLtS, BrLtUn;

  Comparator #(.width(32)) comparator_1 (.a(BrData1), .b(BrData2), .eq(BrEqS), .lt(BrLtS));  // open: gt
  Comparator #(.mode("unsigned"), .width(32)) comparator_2 (
    .a(BrData1), .b(BrData2), .eq(BrEqUn), .lt(BrLtUn));  // open: gt
  Multiplexer multiplexer_1 (.in0(BrEqS), .in1(BrEqUn), .out(BrEq), .sel(BrUn));
  Multiplexer multiplexer_2 (.in0(BrLtS), .in1(BrLtUn), .out(BrLt), .sel(BrUn));

  // Notes on the sheet:
  //   INPUTS to your circuit
  //   DON'T CHANGE THE LOCATIONS OF THE INPUTS AND OUTPUTS!
  //   OUTPUT from your circuit
endmodule
