// Logisim project control-logic.circ as structural Verilog: 1 circuit, main circuit control_logic
module control_logic (
  input  [31:0] Instruction,
  input  BrEq,
  input  BrLt,
  output PCSel,
  output RegWEn,
  output [2:0] ImmSel,
  output BrUn,
  output ASel,
  output BSel,
  output [3:0] ALUSel,
  output MemRW,
  output [1:0] WBSel
);

  wire addi, and_2_out, and_4_out, and_5_out, and_6_out, and_7_out, andi, Arithm_I, Arithm_R, auipc,
       bit_extender_2_out, Branch, decoder_2_out0, decoder_2_out1, decoder_2_out2, decoder_3_out5, jal, jalr,
       Load, lui, not_1_out, not_2_out, not_3_out, not_4_out, not_5_out, not_6_out, not_7_out, not_8_out,
       not_9_out, not_10_out, not_11_out, or_1_out, or_2_out, or_3_out, ori, r_add, r_and, r_mul, r_mulh,
       r_mulhu, r_or, r_sll, r_slt, r_sra, r_srl, r_sub, r_xor, RV32I, slli, slti, srai, srli, Store, xori;
  wire [1:0] bit_extender_1_out;
  wire [5:0] priority_encoder_1_out;
  wire [15:14] rom_1_data;

  and and_1 (RV32I, Instruction[1], Instruction[0]);
  not not_1 (not_1_out, Instruction[6]);
  not not_2 (not_2_out, Instruction[2]);
  not not_3 (not_3_out, Instruction[2]);
  and and_2 (and_2_out, RV32I, not_1_out, not_2_out);
  and and_3 (Branch, RV32I, Instruction[6], not_3_out);
  Decoder #(.select(2)) decoder_1 (
    .out0(Load), .out1(Arithm_I), .out2(Store), .out3(Arithm_R), .sel(Instruction[5:4]), .en(and_2_out));
  Priority_Encoder #(.select_enc(6)) priority_encoder_1 (
    .in0(r_add), .in1(r_mul), .in2(r_sub), .in3(r_sll), .in4(r_mulh), .in5(r_mulhu), .in6(r_slt),
    .in7(r_xor), .in8(r_srl), .in9(r_sra), .in10(r_or), .in11(r_and), .in15(addi), .in16(slli), .in17(slti),
    .in18(xori), .in19(srli), .in20(srai), .in21(ori), .in22(andi), .out(priority_encoder_1_out));  // open: in12, in13, in14, in23, in24, in25, in26, in27, in28, in29, in30, in31, in32, in33, in34, in35, in36, in37, in38, in39, in40, in41, in42, in43, in44, in45, in46, in47, in48, in49, in50, in51, in52, in53, in54, in55, in56, in57, in58, in59, in60, in61, in62, in63, gs, en_out, en_in
  Decoder #(.select(2)) decoder_2 (
    .out0(decoder_2_out0), .out1(decoder_2_out1), .out2(decoder_2_out2),
    .sel({Instruction[30], Instruction[25]}), .en(Arithm_R));  // open: out3
  ROM #(.addrWidth(6), .dataWidth(16)) rom_1 (
    .addr(priority_encoder_1_out), .data({rom_1_data, WBSel, MemRW, ALUSel, BSel, ASel, BrUn, ImmSel, RegWEn}));
  Decoder #(.select(3)) decoder_3 (
    .out0(addi), .out1(slli), .out2(slti), .out4(xori), .out5(decoder_3_out5), .out6(ori), .out7(andi),
    .sel(Instruction[14:12]), .en(Arithm_I));  // open: out3
  Decoder #(.select(3)) decoder_4 (
    .out0(r_add), .out1(r_sll), .out2(r_slt), .out4(r_xor), .out5(r_srl), .out6(r_or), .out7(r_and),
    .sel(Instruction[14:12]), .en(decoder_2_out0));  // open: out3
  Decoder #(.select(2)) decoder_5 (
    .out0(r_mul), .out1(r_mulh), .out3(r_mulhu), .sel(bit_extender_1_out), .en(decoder_2_out1));  // open: out2
  Bit_Extender #(.in_width(3), .out_width(2)) bit_extender_1 (.in(Instruction[14:12]), .out(bit_extender_1_out));
  Decoder decoder_6 (.out0(srli), .out1(srai), .sel(Instruction[30]), .en(decoder_3_out5));
  Decoder decoder_7 (.out0(r_sub), .out1(r_sra), .sel(bit_extender_2_out), .en(decoder_2_out2));
  Bit_Extender #(.in_width(2), .out_width(1)) bit_extender_2 (.in(bit_extender_1_out), .out(bit_extender_2_out));
  not not_4 (not_4_out, BrEq);
  or or_1 (or_1_out, 1'b0, 1'b0);
  or or_2 (or_2_out, 1'b0, 1'b0);
  not not_5 (not_5_out, BrLt);
  and and_4 (and_4_out, 1'b0, BrEq);
  and and_5 (and_5_out, 1'b0, not_4_out);
  and and_6 (and_6_out, or_1_out, BrLt);
  and and_7 (and_7_out, or_2_out, not_5_out);
  not not_6 (not_6_out, Instruction[6]);
  not not_7 (not_7_out, Instruction[5]);
  not not_8 (not_8_out, Instruction[6]);
  or or_3 (or_3_out, and_4_out, and_5_out, and_6_out, and_7_out);
  and and_8 (auipc, RV32I, not_6_out, not_7_out, Instruction[4], Instruction[2]);
  and and_9 (lui, RV32I, not_8_out, Instruction[5], Instruction[4], Instruction[2]);
  or or_4 (PCSel, jal, jalr, or_3_out);
  not not_9 (not_9_out, Instruction[4]);
  not not_10 (not_10_out, Instruction[3]);
  not not_11 (not_11_out, Instruction[4]);
  and and_10 (jalr, RV32I, Instruction[6], Instruction[5], not_9_out, not_10_out, Instruction[2]);
  and and_11 (jal, RV32I, Instruction[6], Instruction[5], not_11_out, Instruction[3], Instruction[2]);

  // Notes on the sheet:
  //   INPUTS to your circuit
  //   DON'T CHANGE THE LOCATIONS OF THE INPUTS AND OUTPUTS!
  //   Determining Instruction Types (U-type and Jumps are not included)
  //   OUTPUT from your circuit
  //   Connect ROM Input here ->
  //   contents of rom_1 (hex, n*v repeats v):
  //   100b 140b 160b 108b 148b 158b 110b 120b 128b 168b 130b 138b 41 41 41 1041 10c1 1141 1241 12c1 16c1
  //   1341 13c1 3842 3842 3842 4*3064 3074 3074 1067 17e7 2069 2041
  //   Determining Instructions
  //   ROM FOR CONTROL LOGIC
  //   This is only if you choose to do the ROM option
  //   CONNECT
  //   WIRE
  //   TO
  //   USE
  //   ROM
  //   Reminder: If using ROM, use combinational logic for PCSel
endmodule
