// Logisim project regfile.circ as structural Verilog: 1 circuit, main circuit regfile
module regfile (
  input  [4:0] ReadIndex1,
  input  [4:0] ReadIndex2,
  input  [4:0] WriteIndex,
  input  [31:0] WriteData,
  input  RegWEn,
  input  clk,
  output [31:0] ra,
  output [31:0] sp,
  output [31:0] t0,
  output [31:0] t1,
  output [31:0] t2,
  output [31:0] s0,
  output [31:0] s1,
  output [31:0] a0,
  output [31:0] ReadData1,
  output [31:0] ReadData2
);

  wire WEa0, WEa1, WEa2, WEa3, WEa4, WEa5, WEa6, WEa7, WEgp, WEra, WEs0, WEs1, WEs2, WEs3, WEs4, WEs5, WEs6,
       WEs7, WEs8, WEs9, WEs10, WEs11, WEsp, WEt0, WEt1, WEt2, WEt3, WEt4, WEt5, WEt6, WEtp, WEx0;
  wire [31:0] a1, a2, a3, a4, a5, a6, a7, gp, s2, s3, s4, s5, s6, s7, s8, s9, s10, s11, t3, t4, t5, t6, tp,
       x0;

  Multiplexer #(.select(5), .width(32)) multiplexer_1 (
    .in0(x0), .in1(ra), .in2(sp), .in3(gp), .in4(tp), .in5(t0), .in6(t1), .in7(t2), .in8(s0), .in9(s1),
    .in10(a0), .in11(a1), .in12(a2), .in13(a3), .in14(a4), .in15(a5), .in16(a6), .in17(a7), .in18(s2),
    .in19(s3), .in20(s4), .in21(s5), .in22(s6), .in23(s7), .in24(s8), .in25(s9), .in26(s10), .in27(s11),
    .in28(t3), .in29(t4), .in30(t5), .in31(t6), .out(ReadData1), .sel(ReadIndex1));
  Multiplexer #(.select(5), .width(32)) multiplexer_2 (
    .in0(x0), .in1(ra), .in2(sp), .in3(gp), .in4(tp), .in5(t0), .in6(t1), .in7(t2), .in8(s0), .in9(s1),
    .in10(a0), .in11(a1), .in12(a2), .in13(a3), .in14(a4), .in15(a5), .in16(a6), .in17(a7), .in18(s2),
    .in19(s3), .in20(s4), .in21(s5), .in22(s6), .in23(s7), .in24(s8), .in25(s9), .in26(s10), .in27(s11),
    .in28(t3), .in29(t4), .in30(t5), .in31(t6), .out(ReadData2), .sel(ReadIndex2));
  Decoder #(.select(5)) decoder_1 (
    .out0(WEx0), .out1(WEra), .out2(WEsp), .out3(WEgp), .out4(WEtp), .out5(WEt0), .out6(WEt1), .out7(WEt2),
    .out8(WEs0), .out9(WEs1), .out10(WEa0), .out11(WEa1), .out12(WEa2), .out13(WEa3), .out14(WEa4),
    .out15(WEa5), .out16(WEa6), .out17(WEa7), .out18(WEs2), .out19(WEs3), .out20(WEs4), .out21(WEs5),
    .out22(WEs6), .out23(WEs7), .out24(WEs8), .out25(WEs9), .out26(WEs10), .out27(WEs11), .out28(WEt3),
    .out29(WEt4), .out30(WEt5), .out31(WEt6), .sel(WriteIndex), .en(RegWEn));
  Register #(.width(32)) register_1 (.D({32{1'b0}}), .en(WEx0), .clk(clk), .Q(x0));  // open: clr
  Register #(.width(32)) register_2 (.D(WriteData), .en(WEra), .clk(clk), .Q(ra));  // open: clr
  Register #(.width(32)) register_3 (.D(WriteData), .en(WEsp), .clk(clk), .Q(sp));  // open: clr
  Register #(.width(32)) register_4 (.D(WriteData), .en(WEgp), .clk(clk), .Q(gp));  // open: clr
  Register #(.width(32)) register_5 (.D(WriteData), .en(WEtp), .clk(clk), .Q(tp));  // open: clr
  Register #(.width(32)) register_6 (.D(WriteData), .en(WEt0), .clk(clk), .Q(t0));  // open: clr
  Register #(.width(32)) register_7 (.D(WriteData), .en(WEt1), .clk(clk), .Q(t1));  // open: clr
  Register #(.width(32)) register_8 (.D(WriteData), .en(WEt2), .clk(clk), .Q(t2));  // open: clr
  Register #(.width(32)) register_9 (.D(WriteData), .en(WEs0), .clk(clk), .Q(s0));  // open: clr
  Register #(.width(32)) register_10 (.D(WriteData), .en(WEs1), .clk(clk), .Q(s1));  // open: clr
  Register #(.width(32)) register_11 (.D(WriteData), .en(WEa0), .clk(clk), .Q(a0));  // open: clr
  Register #(.width(32)) register_12 (.D(WriteData), .en(WEa1), .clk(clk), .Q(a1));  // open: clr
  Register #(.width(32)) register_13 (.D(WriteData), .en(WEa2), .clk(clk), .Q(a2));  // open: clr
  Register #(.width(32)) register_14 (.D(WriteData), .en(WEa3), .clk(clk), .Q(a3));  // open: clr
  Register #(.width(32)) register_15 (.D(WriteData), .en(WEa4), .clk(clk), .Q(a4));  // open: clr
  Register #(.width(32)) register_16 (.D(WriteData), .en(WEa5), .clk(clk), .Q(a5));  // open: clr
  Register #(.width(32)) register_17 (.D(WriteData), .en(WEa6), .clk(clk), .Q(a6));  // open: clr
  Register #(.width(32)) register_18 (.D(WriteData), .en(WEa7), .clk(clk), .Q(a7));  // open: clr
  Register #(.width(32)) register_19 (.D(WriteData), .en(WEs2), .clk(clk), .Q(s2));  // open: clr
  Register #(.width(32)) register_20 (.D(WriteData), .en(WEs3), .clk(clk), .Q(s3));  // open: clr
  Register #(.width(32)) register_21 (.D(WriteData), .en(WEs4), .clk(clk), .Q(s4));  // open: clr
  Register #(.width(32)) register_22 (.D(WriteData), .en(WEs5), .clk(clk), .Q(s5));  // open: clr
  Register #(.width(32)) register_23 (.D(WriteData), .en(WEs6), .clk(clk), .Q(s6));  // open: clr
  Register #(.width(32)) register_24 (.D(WriteData), .en(WEs7), .clk(clk), .Q(s7));  // open: clr
  Register #(.width(32)) register_25 (.D(WriteData), .en(WEs8), .clk(clk), .Q(s8));  // open: clr
  Register #(.width(32)) register_26 (.D(WriteData), .en(WEs9), .clk(clk), .Q(s9));  // open: clr
  Register #(.width(32)) register_27 (.D(WriteData), .en(WEs10), .clk(clk), .Q(s10));  // open: clr
  Register #(.width(32)) register_28 (.D(WriteData), .en(WEs11), .clk(clk), .Q(s11));  // open: clr
  Register #(.width(32)) register_29 (.D(WriteData), .en(WEt3), .clk(clk), .Q(t3));  // open: clr
  Register #(.width(32)) register_30 (.D(WriteData), .en(WEt4), .clk(clk), .Q(t4));  // open: clr
  Register #(.width(32)) register_31 (.D(WriteData), .en(WEt5), .clk(clk), .Q(t5));  // open: clr
  Register #(.width(32)) register_32 (.D(WriteData), .en(WEt6), .clk(clk), .Q(t6));  // open: clr

  // Notes on the sheet:
  //   INPUTS to your circuit
  //   DON'T CHANGE THE LOCATIONS OF THE INPUTS AND OUTPUTS!
  //   These are DEBUG/TEST outputs from your circuit.
  //   Read Selector 1
  //   Read Selector 2
  //   OUTPUTS from your circuit
  //   Write Selector
  //   All 32 Registers
endmodule
